// Logisim project cpu.circ as structural Verilog: 6 circuits, main circuit CPU
module CPU (
  input  [31:0] Instruction,
  input  CLK,
  output [31:0] s0,
  output [31:0] s1,
  output [31:0] t0,
  output [31:0] t1,
  output [31:0] a0,
  output [31:0] ra,
  output [31:0] sp,
  output [31:0] PC
);

  wire Asel, beq, blt, Bsel, incrementer_1_p3, MemRW, PCsel, RegWrEn;
  wire [1:0] Lsel, WBsel;
  wire [2:0] ImmSel;
  wire [3:0] Alusel;
  wire [31:0] ALU, Imm, load_1_out, main_1_p5, multiplexer_1_out, multiplexer_2_out, multiplexer_3_out,
       plus_4, regfile_1_r1, regfile_1_r2, WB;

  Multiplexer #(.width(32), .enable("false")) multiplexer_1 (
    .in0(ALU), .in1(plus_4), .out(multiplexer_1_out), .sel(PCsel));
  // PC pc_1: pin names not known; wires that end beside it: multiplexer_1_out, CLK, PC
  // Incrementer incrementer_1: pin names not known; wires that end beside it: PC, plus_4, incrementer_1_p3
  control control_1 (
    .beq(beq), .in_2(Instruction), .blt(blt), .ImSel(ImmSel), .RegWrEn(RegWrEn), .MemRW(MemRW), .Bsel(Bsel),
    .Asel(Asel), .bun(incrementer_1_p3), .Alusel(Alusel), .WBsel(WBsel), .PCsel(PCsel), .Lsel(Lsel));  // open: Push, Pop, lwc
  RegFile regfile_1 (
    .Clk(CLK), .R1(regfile_1_r1), .R2(regfile_1_r2), .WE(RegWrEn), .W(WB), .RD(PC[11:7]), .RS1(PC[19:15]),
    .RS2(PC[24:20]), .s0(s0), .s1(s1), .t0(t0), .t1(t1), .a0(a0), .ra(ra), .sp(sp));
  // ImmGenerator ImmGenerator: pin names not known; wires that end beside it: PC, ImmSel, Imm
  // BComparator bcomparator_1: pin names not known; wires that end beside it: regfile_1_r1, regfile_1_r1, beq
  Multiplexer #(.width(32), .enable("false")) multiplexer_2 (
    .in0(regfile_1_r1), .in1(PC), .out(multiplexer_2_out), .sel(Asel));
  Multiplexer #(.width(32), .enable("false")) multiplexer_3 (
    .in0(regfile_1_r2), .in1(Imm), .out(multiplexer_3_out), .sel(Bsel));
  ALU alu_1 (.A(multiplexer_2_out), .B(multiplexer_3_out), .ALU_Op(Alusel), .Out(ALU));
  Load load_1 (.In(ALU), .out(load_1_out), .LSel(Lsel));
  // memory_main main_1: pin names not known; wires that end beside it: load_1_out, MemRW, regfile_1_r2, CLK, main_1_p5
  Multiplexer #(.select(2), .width(32), .enable("false")) multiplexer_4 (
    .in0(main_1_p5), .in1(ALU), .in2(plus_4), .in3(Imm), .out(WB), .sel(WBsel));

  // Other names for the same wires on the sheet: fetch_addr[31:0] = PC; rd[4:0] = PC[11:7]; bun = PC[13];
  //   rs1[4:0] = PC[19:15]; rs2[4:0] = PC[24:20]; INST[31:0] = Instruction

  // Notes on the sheet:
  //   NOTE
  //   Please do not modify/replace/move/change/delete/etc input and output pins
  //   These are debug/test outputs from your circuit
endmodule

module ImmGenerator (
  input  [31:0] INSTRUCTION,
  input  [2:0] ImmSel,
  output [31:0] Immediate
);

  wire [11:0] bit_extender_4_out;
  wire [19:0] bit_extender_3_out;
  wire [20:0] bit_extender_1_out, bit_extender_2_out;
  wire [31:0] bit_extender_5_out;

  assign bit_extender_1_out = {{20{1'b0}}, INSTRUCTION[31]};  // Bit_Extender bit_extender_1
  assign bit_extender_2_out = {{20{1'b0}}, INSTRUCTION[31]};  // Bit_Extender bit_extender_2
  assign bit_extender_3_out = {{19{1'b0}}, INSTRUCTION[31]};  // Bit_Extender bit_extender_3
  assign bit_extender_4_out = {{11{1'b0}}, INSTRUCTION[31]};  // Bit_Extender bit_extender_4
  assign bit_extender_5_out = {{25{1'b0}}, INSTRUCTION[31:25]};  // Bit_Extender bit_extender_5
  Multiplexer #(.select(3), .width(32), .enable("false")) multiplexer_1 (
    .in0({bit_extender_1_out, INSTRUCTION[30:20]}),
    .in1({bit_extender_2_out, INSTRUCTION[30:25], INSTRUCTION[11:7]}),
    .in2({bit_extender_3_out, INSTRUCTION[7], INSTRUCTION[30:25], INSTRUCTION[11:8], 1'b0}),
    .in3({INSTRUCTION[31:12], {12{1'b0}}}),
    .in4({bit_extender_4_out, INSTRUCTION[19:12], INSTRUCTION[20], INSTRUCTION[30:21], 1'b0}),
    .in5(bit_extender_5_out), .out(Immediate), .sel(ImmSel));  // open: in6, in7

  // Other names for the same wires on the sheet: funct7[6:0] = INSTRUCTION[31:25]; funct3[2:0] = INSTRUCTION[14:12];
  //   opcode[6:0] = INSTRUCTION[6:0]
endmodule

module BComparator (
  input  [31:0] A,
  input  [31:0] B,
  input  bun,
  output beq,
  output blt
);

  wire comparator_1_eq, comparator_1_lt, comparator_2_eq, comparator_2_lt;

  Comparator #(.width(32)) comparator_1 (.a(A), .b(B), .eq(comparator_1_eq), .lt(comparator_1_lt));  // open: gt
  Comparator #(.width(32)) comparator_2 (.a(A), .b(B), .eq(comparator_2_eq), .lt(comparator_2_lt));  // open: gt
  Multiplexer multiplexer_1 (.in0(comparator_1_eq), .in1(comparator_2_eq), .out(beq), .sel(bun));  // open: en
  Multiplexer multiplexer_2 (.in0(comparator_1_lt), .in1(comparator_2_lt), .out(blt), .sel(bun));  // open: en
endmodule

module control (
  input  beq,
  input  [31:0] in_2,
  input  blt,
  output [1:0] Lsel,
  output [2:0] ImSel,
  output RegWrEn,
  output Push,
  output MemRW,
  output Bsel,
  output Pop,
  output Asel,
  output bun,
  output lwc,
  output [3:0] Alusel,
  output [1:0] WBsel,
  output PCsel
);

  wire and_2_out, and_3_out, and_4_out, and_5_out, BranchCode, Btype, comparator_2_eq, comparator_3_eq,
       comparator_4_eq, comparator_9_eq, comparator_10_eq, comparator_11_eq, comparator_12_eq,
       comparator_13_eq, comparator_14_eq, comparator_15_eq, comparator_16_eq, comparator_17_eq,
       comparator_18_eq, comparator_19_eq, comparator_20_eq, comparator_21_eq, comparator_22_eq,
       comparator_23_eq, comparator_24_eq, Itype, Jtype, not_1_out, or_2_out, or_3_out, or_6_out, or_7_out,
       or_9_out, or_11_out, Stype, Utype;
  wire [0:0] or_10_out;
  wire [1:0] bit_extender_1_out, bit_extender_2_out, multiplier_1_out;
  wire [4:0] multiplexer_1_out;

  Comparator #(.width(7)) comparator_1 (.a(in_2[6:0]), .b(7'b0110011), .eq(Bsel));  // open: gt, lt
  Comparator #(.width(7)) comparator_2 (.a(in_2[6:0]), .b(7'b0000011), .eq(comparator_2_eq));  // open: gt, lt
  Comparator #(.width(7)) comparator_3 (.a(in_2[6:0]), .b(7'b0010011), .eq(comparator_3_eq));  // open: gt, lt
  Comparator #(.width(7)) comparator_4 (.a(in_2[6:0]), .b(7'b1100111), .eq(comparator_4_eq));  // open: gt, lt
  Comparator #(.width(7)) comparator_5 (.a(in_2[6:0]), .b(7'b0100011), .eq(Stype));  // open: gt, lt
  Comparator #(.width(7)) comparator_6 (.a(in_2[6:0]), .b(7'b1100011), .eq(Btype));  // open: gt, lt
  Comparator #(.width(7)) comparator_7 (.a(in_2[6:0]), .b(7'b0110111), .eq(Utype));  // open: gt, lt
  Comparator #(.width(7)) comparator_8 (.a(in_2[6:0]), .b(7'b1101111), .eq(Jtype));  // open: gt, lt
  and and_1 (bun, Btype, in_2[13]);
  Comparator #(.width(5)) comparator_9 (.a(in_2[6:2]), .b({5{1'b0}}), .eq(comparator_9_eq));  // open: gt, lt
  Comparator #(.width(7)) comparator_10 (.a(in_2[6:0]), .b(7'b1101111), .eq(comparator_10_eq));  // open: gt, lt
  Comparator #(.width(7)) comparator_11 (.a(in_2[6:0]), .b(7'b1100111), .eq(comparator_11_eq));  // open: gt, lt
  Comparator #(.width(3)) comparator_12 (.a(in_2[14:12]), .b(3'b000), .eq(comparator_12_eq));  // open: gt, lt
  Comparator #(.width(3)) comparator_13 (.a(in_2[14:12]), .b(3'b100), .eq(comparator_13_eq));  // open: gt, lt
  Comparator #(.width(3)) comparator_14 (.a(in_2[14:12]), .b(3'b110), .eq(comparator_14_eq));  // open: gt, lt
  Comparator #(.width(3)) comparator_15 (.a(in_2[14:12]), .b(3'b001), .eq(comparator_15_eq));  // open: gt, lt
  not not_1 (not_1_out, beq);
  or or_1 (Itype, comparator_2_eq, comparator_3_eq, comparator_4_eq);
  assign bit_extender_1_out = {{1{1'b0}}, comparator_9_eq};  // Bit_Extender bit_extender_1
  assign bit_extender_2_out = {{1{1'b0}}, or_2_out};  // Bit_Extender bit_extender_2
  or or_2 (or_2_out, comparator_10_eq, comparator_11_eq);
  and and_2 (and_2_out, comparator_12_eq, beq);
  and and_3 (and_3_out, comparator_13_eq, blt);
  and and_4 (and_4_out, comparator_14_eq, blt);
  and and_5 (and_5_out, comparator_15_eq, not_1_out);
  or or_3 (or_3_out, Stype, Btype);
  or or_4 (MemRW, Stype, Push);
  or or_5 (Asel, Bsel, or_6_out);
  or or_6 (or_6_out, Stype, Itype);
  ALUsel alusel_1 (.Alusel(Alusel));  // open: in_1
  Multiplier #(.width(2)) multiplier_1 (.a(2'b10), .b(bit_extender_2_out), .out(multiplier_1_out));  // open: cin, cout
  or or_7 (or_7_out, and_2_out, and_3_out);
  or or_8 (BranchCode, or_7_out, or_9_out);
  or or_9 (or_9_out, and_4_out, and_5_out);
  or or_10 (or_10_out[0], Pop, Itype);
  not not_2 (RegWrEn, or_3_out);
  Adder #(.width(2)) adder_1 (.a(bit_extender_1_out), .b(multiplier_1_out), .out(WBsel));  // open: cin, cout
  Multiplexer #(.width(5)) multiplexer_1 (
    .in0({Jtype, Utype, Btype, Stype, or_10_out[0]}), .in1({5{1'b0}}), .out(multiplexer_1_out), .sel(lwc));  // open: en
  Comparator #(.width(7)) comparator_16 (.a(in_2[6:0]), .b(7'b0111011), .eq(comparator_16_eq));  // open: gt, lt
  Comparator #(.width(3)) comparator_17 (.a(in_2[14:12]), .b(3'b011), .eq(comparator_17_eq));  // open: gt, lt
  Comparator #(.width(7)) comparator_18 (.a(in_2[6:0]), .b(7'b0111011), .eq(comparator_18_eq));  // open: gt, lt
  Comparator #(.width(3)) comparator_19 (.a(in_2[14:12]), .b(3'b010), .eq(comparator_19_eq));  // open: gt, lt
  Multiplexer #(.select(5), .width(3)) multiplexer_2 (
    .in0(3'b101), .in1(3'b000), .in2(3'b001), .in4(3'b010), .in8(3'b011), .in16(3'b100), .out(ImSel),
    .sel(multiplexer_1_out));  // open: in3, in5, in6, in7, in9, in10, in11, in12, in13, in14, in15, in17, in18, in19, in20, in21, in22, in23, in24, in25, in26, in27, in28, in29, in30, in31, en
  Comparator #(.width(7)) comparator_20 (.a(in_2[6:0]), .b(7'b0000011), .eq(comparator_20_eq));  // open: gt, lt
  Comparator #(.width(3)) comparator_21 (.a(in_2[14:12]), .b(3'b111), .eq(comparator_21_eq));  // open: gt, lt
  and and_6 (Push, comparator_16_eq, comparator_17_eq);
  and and_7 (Pop, comparator_18_eq, comparator_19_eq);
  and and_8 (lwc, comparator_20_eq, comparator_21_eq);
  Comparator #(.width(7)) comparator_22 (.a(in_2[6:0]), .b(7'b1101111), .eq(comparator_22_eq));  // open: gt, lt
  Comparator #(.width(7)) comparator_23 (.a(in_2[6:0]), .b(7'b1100111), .eq(comparator_23_eq));  // open: gt, lt
  Comparator #(.width(7)) comparator_24 (.a(in_2[6:0]), .b(7'b1100011), .eq(comparator_24_eq));  // open: gt, lt
  or or_11 (or_11_out, comparator_22_eq, comparator_23_eq);
  Multiplexer multiplexer_3 (.in0(or_11_out), .in1(BranchCode), .out(PCsel), .sel(comparator_24_eq));  // open: en

  assign Lsel = in_2[13:12];

  // Other names for the same wires on the sheet: opcode[6:0] = in_2[6:0]; funct3[2:0] = in_2[14:12];
  //   funct7[6:0] = in_2[31:25]; pc = PCsel; Rtype = Bsel
endmodule

module ALUsel (
  input  [31:0] in_1,
  output [3:0] Alusel
);

  wire and_1_out, comparator_6_eq, comparator_11_eq, comparator_12_eq;
  wire [1:0] comparator_4_eq, ControlFunct7;
  wire [2:0] comparator_1_eq;
  wire [3:0] AMS, comparator_7_eq, DSS, I, IFunctSel, multiplexer_3_out, R, RA, RFunctSel, SM;

  Comparator #(.width(7)) comparator_1 (.a(in_1[31:25]), .b({7{1'b0}}), .eq(comparator_1_eq[0]));  // open: gt, lt
  Comparator #(.width(7)) comparator_2 (.a(in_1[31:25]), .b(7'b0000001), .eq(comparator_1_eq[1]));  // open: gt, lt
  Comparator #(.width(7)) comparator_3 (.a(in_1[31:25]), .b(7'b0100000), .eq(comparator_1_eq[2]));  // open: gt, lt
  Multiplexer #(.select(3), .width(4)) multiplexer_1 (
    .in0(4'b0000), .in1(4'b0110), .in2(4'b0111), .in3(4'b1011), .in4(4'b0011), .in5(4'b0101), .in6(4'b0010),
    .in7(4'b0001), .out(RFunctSel), .sel(in_1[14:12]));  // open: en
  Multiplexer #(.select(3), .width(4)) multiplexer_2 (
    .in0(4'b0000), .in1(4'b0110), .in2(4'b0111), .in4(4'b0011), .in5(4'b0101), .in6(4'b0010), .in7(4'b0001),
    .out(IFunctSel), .sel(in_1[14:12]));  // open: in3, en
  Comparator #(.width(7)) comparator_4 (.a(in_1[6:0]), .b(7'b0010011), .eq(comparator_4_eq[0]));  // open: gt, lt
  Comparator #(.width(7)) comparator_5 (.a(in_1[6:0]), .b(7'b0110011), .eq(comparator_4_eq[1]));  // open: gt, lt
  Comparator #(.width(7)) comparator_6 (.a(in_1[6:0]), .b(7'b0110111), .eq(comparator_6_eq));  // open: gt, lt
  Multiplexer #(.select(2), .width(4)) multiplexer_3 (
    .in0(4'b0000), .in1(I), .in2(R), .out(multiplexer_3_out), .sel(comparator_4_eq));  // open: in3, en
  Multiplexer #(.select(3), .width(2)) multiplexer_4 (
    .in1(2'b00), .in2(2'b01), .in4(2'b10), .out(ControlFunct7), .sel(comparator_1_eq));  // open: in0, in3, in5, in6, in7, en
  Multiplexer #(.select(2), .width(4)) multiplexer_5 (
    .in0(4'b0000), .in1(4'b1010), .in2(4'b1100), .out(AMS), .sel(ControlFunct7));  // open: in3, en
  Multiplexer #(.select(2), .width(4)) multiplexer_6 (
    .in0(4'b0110), .in1(4'b1011), .out(SM), .sel(ControlFunct7));  // open: in2, in3, en
  Multiplexer #(.width(4)) multiplexer_7 (
    .in0(multiplexer_3_out), .in1(4'b1101), .out(Alusel), .sel(comparator_6_eq));  // open: en
  Comparator #(.width(4)) comparator_7 (.a(RFunctSel), .b(4'b0000), .eq(comparator_7_eq[0]));  // open: gt, lt
  Comparator #(.width(4)) comparator_8 (.a(RFunctSel), .b(4'b0110), .eq(comparator_7_eq[1]));  // open: gt, lt
  Comparator #(.width(4)) comparator_9 (.a(RFunctSel), .b(4'b0101), .eq(comparator_7_eq[2]));  // open: gt, lt
  Comparator #(.width(4)) comparator_10 (.a(RFunctSel), .b(4'b0001), .eq(comparator_7_eq[3]));  // open: gt, lt
  Comparator #(.width(4)) comparator_11 (.a(IFunctSel), .b(4'b0101), .eq(comparator_11_eq));  // open: gt, lt
  Comparator #(.width(7)) comparator_12 (.a(in_1[31:25]), .b({7{1'b0}}), .eq(comparator_12_eq));  // open: gt, lt
  Multiplexer #(.select(2), .width(4)) multiplexer_8 (
    .in0(4'b0100), .in1(4'b1000), .in2(4'b0101), .out(DSS), .sel(ControlFunct7));  // open: in3, en
  Multiplexer #(.select(2), .width(4)) multiplexer_9 (
    .in0(4'b0001), .in1(4'b1001), .out(RA), .sel(ControlFunct7));  // open: in2, in3, en
  and and_1 (and_1_out, comparator_11_eq, comparator_12_eq);
  Multiplexer #(.select(4), .width(4)) multiplexer_10 (
    .in0(RFunctSel), .in1(AMS), .in2(SM), .in4(DSS), .in8(RA), .out(R), .sel(comparator_7_eq));  // open: in3, in5, in6, in7, in9, in10, in11, in12, in13, in14, in15, en
  Multiplexer #(.width(4)) multiplexer_11 (.in0(IFunctSel), .in1(4'b0100), .out(I), .sel(and_1_out));  // open: en

  // Other names for the same wires on the sheet: opcode[6:0] = in_1[6:0]; funct3[2:0] = in_1[14:12];
  //   funct7[6:0] = in_1[31:25]
endmodule

module Load (
  input  [1:0] LSel,
  input  [31:0] In,
  output [31:0] out
);

  wire [31:0] bit_extender_1_out, bit_extender_2_out;

  assign bit_extender_1_out = {{24{1'b0}}, In[7:0]};  // Bit_Extender bit_extender_1
  assign bit_extender_2_out = {{16{1'b0}}, In[15:0]};  // Bit_Extender bit_extender_2
  Multiplexer #(.select(2), .width(32), .enable("false")) multiplexer_1 (
    .in0(bit_extender_1_out), .in1(bit_extender_2_out), .in2(In), .out(out), .sel(LSel));  // open: in3
endmodule
