// Logisim project regfile.circ as structural Verilog: 1 circuit, main circuit RegFile
module RegFile (
  input  [4:0] RD,
  input  [4:0] RS1,
  input  [4:0] RS2,
  input  [31:0] W,
  input  WE,
  input  Clk,
  output [31:0] s0,
  output [31:0] s1,
  output [31:0] t0,
  output [31:0] t1,
  output [31:0] a0,
  output [31:0] ra,
  output [31:0] sp,
  output [31:0] R1,
  output [31:0] R2
);

  wire demultiplexer_1_out0, demultiplexer_1_out2, demultiplexer_1_out4, demultiplexer_1_out6,
       demultiplexer_1_out8, demultiplexer_1_out10, demultiplexer_1_out12, demultiplexer_1_out14;
  wire [31:0] a1, zero;

  Demultiplexer #(.select(5)) demultiplexer_1 (
    .out0(demultiplexer_1_out0), .out2(demultiplexer_1_out2), .out4(demultiplexer_1_out4),
    .out6(demultiplexer_1_out6), .out8(demultiplexer_1_out8), .out10(demultiplexer_1_out10),
    .out12(demultiplexer_1_out12), .out14(demultiplexer_1_out14), .in(WE), .sel(RD));  // open: out1, out3, out5, out7, out9, out11, out13, out15, out16, out17, out18, out19, out20, out21, out22, out23, out24, out25, out26, out27, out28, out29, out30, out31, en
  Register #(.width(32)) u_zero (.en(1'b0), .Q(zero));  // open: D, clk, clr
  Register #(.width(32)) u_ra (.D(W), .en(demultiplexer_1_out0), .Q(ra), .clk(Clk));  // open: clr
  Register #(.width(32)) u_sp (.D(W), .en(demultiplexer_1_out2), .Q(sp), .clk(Clk));  // open: clr
  Register #(.width(32)) u_t0 (.D(W), .en(demultiplexer_1_out4), .Q(t0), .clk(Clk));  // open: clr
  Register #(.width(32)) u_t1 (.D(W), .en(demultiplexer_1_out6), .Q(t1), .clk(Clk));  // open: clr
  Register #(.width(32)) u_s0 (.D(W), .en(demultiplexer_1_out8), .Q(s0), .clk(Clk));  // open: clr
  Register #(.width(32)) u_s1 (.D(W), .en(demultiplexer_1_out10), .Q(s1), .clk(Clk));  // open: clr
  Register #(.width(32)) u_a0 (.D(W), .en(demultiplexer_1_out12), .Q(a0), .clk(Clk));  // open: clr
  Register #(.width(32)) u_a1 (.D(W), .en(demultiplexer_1_out14), .Q(a1), .clk(Clk));  // open: clr
  Multiplexer #(.select(5), .width(32)) multiplexer_1 (
    .in8(zero), .in10(ra), .in12(sp), .in14(t0), .in16(t1), .in18(s0), .in21(s1), .in27(a0), .in30(a1),
    .out(R1), .sel(RS1));  // open: in0, in1, in2, in3, in4, in5, in6, in7, in9, in11, in13, in15, in17, in19, in20, in22, in23, in24, in25, in26, in28, in29, in31, en
  Multiplexer #(.select(5), .width(32)) multiplexer_2 (
    .in8(zero), .in10(ra), .in12(sp), .in14(t0), .in16(t1), .in18(s0), .in20(s1), .in22(a0), .in23(a1),
    .out(R2), .sel(RS2));  // open: in0, in1, in2, in3, in4, in5, in6, in7, in9, in11, in13, in15, in17, in19, in21, in24, in25, in26, in27, in28, in29, in30, in31, en

  // Notes on the sheet:
  //   Write Register
  //   Read Register 1
  //   Read Register 2
  //   Write Data
  //   Write Enable
  //   Clock
  //   NOTE
  //   Please do not modify/replace/move/change/delete/etc input and output pins
  //   These are debug/test outputs from your circuit
  //   Read Data 1
  //   Read Data 2
endmodule
